# Fritzing sketch pico-ledstrip-strip (saved by Fritzing 0.9.10b)
breadboards: 1

parts:
  Mod1 = Raspberry Pi Pico W
  R3 = Resistor [tolerance=±5% resistance=100k package="0805 [SMD]"]
  R4 = Resistor [tolerance=±5% resistance=100k package="0805 [SMD]"]
  R5 = Resistor [tolerance=±5% resistance=100k package="0805 [SMD]"]
  Q1 = Basic FET N-Channel [package="TO220 [THT]"]
  Q2 = Basic FET N-Channel [package="TO220 [THT]"]
  Q3 = Basic FET N-Channel [package="TO220 [THT]"]
  A1 = Hanmatek HM305
  A2 = RGB Strip LED

nets:
  N1: Mod1.pin_3, Mod1.pin_8, Mod1.pin_13, Mod1.pin_18, Mod1.pin_23, Mod1.pin_28, Mod1.pin_33, Mod1.pin_38, Mod1.pin_42, R3.Pin_0, R4.Pin_0, R5.Pin_0, Q1.source, Q2.source, Q3.source, A1.Pin_3
  N2: Mod1.pin_31, R4.Pin_1, Q1.gate
  N3: Mod1.pin_32, R5.Pin_1, Q2.gate
  N4: Mod1.pin_34, R3.Pin_1, Q3.gate
  N5: Q1.drain, A2.Red_Connect
  N6: Q2.drain, A2.Green_Connect
  N7: Q3.drain, A2.Blue_Connect
  N8: A1.Pin_4, A2.Common_Connect

custom parts:
  Raspberry Pi Pico W: Raspberry Pi Pico W. Based around the RP2040 microcontroller the Pico W is a low cost microcontroller device bringing Raspberry Pi quality, cost, and easy of use to the microcontroller space. The areas marked KEEPOUT in pcb silkscreen should not have traces running through them to avoid shorts on a soldered in module!
  Hanmatek HM305: DC Power Supply 30V5A HM305.
  RGB Strip LED: A tri-color Strip LED with red, green and blue. Pin order: red - common cathode - blue - green
